# Fritzing sketch inet_power (saved by Fritzing 1.0.2b)

parts:
  MCU1 = Raspberry Pi Zero
  J1 = Power Jack [package=power_jack_pth_lock]
  M1 = RioRand LM2596
  S1 = Round Pushbutton
  U1 = RELAY [package=relay-g5q]
  U2 = RELAY [package=relay-g5q]
  U3 = RELAY [package=relay-g5q]
  J2 = Power Jack [package=power_jack_pth_lock]
  J3 = Power Jack [package=power_jack_pth_lock]
  J4 = Power Jack [package=power_jack_pth_lock]

nets:
  N1: MCU1.pin_2, MCU1.pin_4, M1.Pin_3
  N2: MCU1.pin_6, MCU1.pin_39, M1.Pin_4
  N3: MCU1.pin_11, S1.leg0
  N4: MCU1.pin_13, U1.COIL1
  N5: MCU1.pin_15, U2.COIL1
  N6: MCU1.pin_16, U3.COIL1
  N7: J1.GND, M1.Pin_2, S1.leg1
  N8: J1.PWR, M1.Pin_1, U1.MAIN, U2.MAIN, U3.MAIN
  N9: U1.NO, J4.PWR
  N10: U2.NO, J3.PWR
  N11: U3.NO, J2.PWR
  GND: J2.GND, J3.GND, J4.GND
